# Fritzing sketch arduino_luna_alarm (saved by Fritzing 0.9.2b)
breadboards: 1

parts:
  Part1 = Arduino Nano (Rev3.0)
  SP1 = SPEAKER [package=pcb_mount_speaker]
  C1 = Electrolytic Capacitor [capacitance=100µF package="200 mil [THT, electrolytic]"]
  PIR1 = PIR sensor
  Power_plug1_5V = Power plug

nets:
  GND: Part1.GND, C1.-, PIR1.GND, Power_plug1_5V.GND
  N1: Part1.D3, SP1.-
  N2: Part1.D4, PIR1.SIG
  VIN: Part1.VIN, Power_plug1_5V.VCC
  3V3: Part1.3V3, PIR1.VDD
  N3: SP1.+, C1.+
